// Logisim project beta_machine.circ as structural Verilog: 12 circuits, main circuit main
module ALU (
  input  [31:0] A,
  input  [31:0] B,
  input  [3:0] RA1,
  output [31:0] OUT
);

  wire [31:0] adder_1_out, and_1_out, divider_1_out, enhanced_comparator_1_out_5,
       enhanced_comparator_1_out_6, enhanced_comparator_1_out_7, multiplier_1_out, or_1_out, shifter_1_out,
       shifter_2_out, shifter_3_out, subtractor_1_out, xor_1_out;

  Multiplier #(.width(32)) multiplier_1 (.a(A), .b(B), .out(multiplier_1_out));  // open: cin, cout
  Subtractor #(.width(32)) subtractor_1 (.a(A), .b(B), .out(subtractor_1_out));  // open: bin, bout
  Adder #(.width(32)) adder_1 (.a(A), .b(B), .out(adder_1_out));  // open: cin, cout
  Divider #(.width(32)) divider_1 (.a(A), .b(B), .out(divider_1_out));  // open: upper, rem
  assign and_1_out = A & B;  // AND_Gate and_1, 32 bits wide
  assign or_1_out = A | B;  // OR_Gate or_1, 32 bits wide
  Multiplexer #(.select(4), .width(32), .enable("false")) multiplexer_1 (
    .in1(adder_1_out), .in2(subtractor_1_out), .in3(multiplier_1_out), .in4(divider_1_out), .in5(and_1_out),
    .in6(or_1_out), .in7(xor_1_out), .in8(enhanced_comparator_1_out_6), .in9(enhanced_comparator_1_out_7),
    .in10(enhanced_comparator_1_out_5), .in11(shifter_3_out), .in12(shifter_2_out), .in13(shifter_1_out),
    .out(OUT), .sel(RA1));  // open: in0, in14, in15
  assign xor_1_out = A ^ B;  // XOR_Gate xor_1, 32 bits wide
  enhanced_comparator enhanced_comparator_1 (
    .Input_1(A), .Input_2(B), .out_5(enhanced_comparator_1_out_5), .out_6(enhanced_comparator_1_out_6),
    .out_7(enhanced_comparator_1_out_7));  // open: out_3, out_4
  Shifter #(.width(32), .shift("ar")) shifter_1 (.in(A), .\dist (B[4:0]), .out(shifter_1_out));
  Shifter #(.width(32), .shift("lr")) shifter_2 (.in(A), .\dist (B[4:0]), .out(shifter_2_out));
  Shifter #(.width(32)) shifter_3 (.in(A), .\dist (B[4:0]), .out(shifter_3_out));

  // Notes on the sheet:
  //   ALUFN specifies the operation
endmodule

module enhanced_comparator (
  input  [31:0] Input_1,
  input  [31:0] Input_2,
  output [31:0] out_3,
  output [31:0] out_4,
  output [31:0] out_5,
  output [31:0] out_6,
  output [31:0] out_7
);

  Comparator #(.width(32)) comparator_1 (.a(Input_1), .b(Input_2), .gt(out_4[0]), .eq(out_5[0]), .lt(out_6[0]));
  assign out_3 = {{31{1'b0}}, out_4[0]} | {{31{1'b0}}, out_5[0]};  // OR_Gate or_1, 32 bits wide
  assign out_7 = {{31{1'b0}}, out_5[0]} | {{31{1'b0}}, out_6[0]};  // OR_Gate or_2, 32 bits wide

  assign out_4[31:1] = {31{1'b0}};
  assign out_5[31:1] = {31{1'b0}};
  assign out_6[31:1] = {31{1'b0}};
endmodule

module program_counter (
  input  [31:0] In,
  input  Reset,
  output [31:0] Out
);

  wire Clock_out;
  wire [31:0] multiplexer_1_out;

  Multiplexer #(.width(32), .enable("false")) multiplexer_1 (
    .in0(In), .in1({32{1'b0}}), .out(multiplexer_1_out), .sel(Reset));
  Clock Clock (.out(Clock_out));
  Register #(.width(32)) register_1 (.D(multiplexer_1_out), .Q(Out), .clk(Clock_out));  // open: en, clr
endmodule

module register_file (
  input  WE,
  input  [4:0] WA,
  input  [31:0] WD,
  input  [4:0] RA1,
  input  [4:0] RA2,
  output [31:0] RD1,
  output [31:0] RD2
);

  wire clock_1_out, demultiplexer_1_out0, demultiplexer_1_out1, demultiplexer_1_out2, demultiplexer_1_out3,
       demultiplexer_1_out4, demultiplexer_1_out30, demultiplexer_1_out31;
  wire [31:0] r0_q, r1_q, r2_q, r3_q, r4_q, r29_q, r30_q;

  Multiplexer #(.select(5), .width(32), .enable("false")) multiplexer_1 (
    .in0(r0_q), .in1(r1_q), .in2(r2_q), .in3(r3_q), .in4(r4_q), .in29(r29_q), .in30(r30_q),
    .in31({32{1'b0}}), .out(RD1), .sel(RA1));  // open: in5, in6, in7, in8, in9, in10, in11, in12, in13, in14, in15, in16, in17, in18, in19, in20, in21, in22, in23, in24, in25, in26, in27, in28
  Register #(.width(32)) r0 (.D(WD), .en(demultiplexer_1_out0), .Q(r0_q), .clk(clock_1_out));  // open: clr
  Clock clock_1 (.out(clock_1_out));
  Demultiplexer #(.select(5), .enable("false")) demultiplexer_1 (
    .out0(demultiplexer_1_out0), .out1(demultiplexer_1_out1), .out2(demultiplexer_1_out2),
    .out3(demultiplexer_1_out3), .out4(demultiplexer_1_out4), .out30(demultiplexer_1_out30),
    .out31(demultiplexer_1_out31), .in(WE), .sel(WA));  // open: out5, out6, out7, out8, out9, out10, out11, out12, out13, out14, out15, out16, out17, out18, out19, out20, out21, out22, out23, out24, out25, out26, out27, out28, out29
  Register #(.width(32)) r1 (.D(WD), .en(demultiplexer_1_out1), .Q(r1_q), .clk(clock_1_out));  // open: clr
  Register #(.width(32)) r2 (.D(WD), .en(demultiplexer_1_out2), .Q(r2_q), .clk(clock_1_out));  // open: clr
  Register #(.width(32)) r3 (.D(WD), .en(demultiplexer_1_out3), .Q(r3_q), .clk(clock_1_out));  // open: clr
  Register #(.width(32)) r4 (.D(WD), .en(demultiplexer_1_out4), .Q(r4_q), .clk(clock_1_out));  // open: clr
  Multiplexer #(.select(5), .width(32), .enable("false")) multiplexer_2 (
    .in0(r0_q), .in1(r1_q), .in2(r2_q), .in3(r3_q), .in4(r4_q), .in29(r29_q), .in30(r30_q),
    .in31({32{1'b0}}), .out(RD2), .sel(RA2));  // open: in5, in6, in7, in8, in9, in10, in11, in12, in13, in14, in15, in16, in17, in18, in19, in20, in21, in22, in23, in24, in25, in26, in27, in28
  Register #(.width(32)) r30 (.D(WD), .en(demultiplexer_1_out31), .Q(r30_q), .clk(clock_1_out));  // open: clr
  Register #(.width(32)) r29 (.D(WD), .en(demultiplexer_1_out30), .Q(r29_q), .clk(clock_1_out));  // open: clr

  // Notes on the sheet:
  //   - WA (in) register address for writing
  //   - RA1 (in) first register address for reading
  //   - RA2 (in) second register address for reading
  //   - WD (in) data to write in register addressed by WA
  //   - WE (in) enable writing (1) or not (0), at the next clock trigger
  //   - RD1 (out) data in register addressed by RA1
  //   - RD2 (out) data in register addressed by RA2
endmodule

module instruction_memory (
  input  [31:0] In,
  output [31:0] Out
);

  ROM #(.dataWidth(32)) rom_1 (.addr(In[9:2]), .data(Out));  // open: sel

  // Notes on the sheet:
  //   contents of rom_1 (hex, n*v repeats v):
  //   c01f0002 c4000001 c8000002 cc000002 e4200003 e8200003 e0200003 f0000001 f4000001 c05f0038 6c820000
  //   c8420000 c0420001 c0420001 8842f800 c0420003 c0420001 8800f800 8821f800 8842f800 8884f800 c01f0003
  //   641f0000 77ff0000 c05f0001 603f0000 77e10003 88420800 c4210001 77fffffc 645f0004
endmodule

module main (
  input  Reset
);

  wire BSEL, RA2SEL, WERF, WR, Z;
  wire [1:0] PCSEL, WDSEL;
  wire [3:0] ALUFN;
  wire [4:0] multiplexer_2_out, Ra, Rc;
  wire [5:0] OPCODE;
  wire [15:0] lit;
  wire [31:0] adder_1_out, alu_1_out, data_memory_1_rd, JT, multiplexer_1_out, multiplexer_3_out,
       multiplexer_4_out, plus_4, program_counter_1_out, register_file_1_rd2, sext_1_sext, sext_2_sext,
       x4_1_out;

  sext sext_1 (.lit(lit), .sext(sext_1_sext));
  x4 x4_1 (.in(sext_1_sext), .out(x4_1_out));
  Adder #(.width(32)) adder_1 (.a(x4_1_out), .b(plus_4), .out(adder_1_out));  // open: cin, cout
  Multiplexer #(.select(2), .width(32), .enable("false")) multiplexer_1 (
    .in0(plus_4), .in1(adder_1_out), .in2(JT), .out(multiplexer_1_out), .sel(PCSEL));  // open: in3
  program_counter program_counter_1 (.Out(program_counter_1_out), .Reset(Reset), .In(multiplexer_1_out));
  _4 u_4_1 (.in(program_counter_1_out), .out(plus_4));
  instruction_memory instruction_memory_1 (.In(program_counter_1_out), .Out({OPCODE, Rc, Ra, lit}));
  ORing_negation oring_negation_1 (.RD1(JT), .Z(Z));
  ALU alu_1 (.RA1(ALUFN), .A(JT), .B(multiplexer_3_out), .OUT(alu_1_out));
  Multiplexer #(.width(5), .enable("false")) multiplexer_2 (
    .in0(lit[15:11]), .in1(Rc), .out(multiplexer_2_out), .sel(RA2SEL));
  register_file register_file_1 (
    .WA(Rc), .WE(WERF), .WD(multiplexer_4_out), .RA1(Ra), .RA2(multiplexer_2_out), .RD1(JT),
    .RD2(register_file_1_rd2));
  sext sext_2 (.lit(lit), .sext(sext_2_sext));
  Multiplexer #(.width(32), .enable("false")) multiplexer_3 (
    .in0(sext_2_sext), .in1(register_file_1_rd2), .out(multiplexer_3_out), .sel(BSEL));
  Multiplexer #(.select(2), .width(32), .enable("false")) multiplexer_4 (
    .in0(plus_4), .in1(alu_1_out), .in2(data_memory_1_rd), .out(multiplexer_4_out), .sel(WDSEL));  // open: in3
  data_memory data_memory_1 (.Addr(alu_1_out), .WD(register_file_1_rd2), .RD(data_memory_1_rd), .R_W(WR));
  control_logic control_logic_1 (.Opcode(OPCODE), .Out({ALUFN, WERF, BSEL, WDSEL, WR, RA2SEL, PCSEL}), .Z(Z));

  // Other names for the same wires on the sheet: Rb[4:0] = lit[15:11]

  // Notes on the sheet:
  //   15:0
  //   - Ra first register addres for reading
  //   - Rb second register addres for reading
  //   - Rc register addres for writing
  //   - ALUFN operation done by the ALU
  //   - JT is the content of register Ra as output on RD1
  //   31:26
  //   25:21
  //   - WERF enables writing in a register (1) or not (0) at the next clock trigger
  //   - WR enables (1) or not (0) writing in the memory (at the next clock trigger)
  //   - Z is simply computed by ORing all bits of Ra, and taking the negation
  //   15:0
  //   20:16
  //   - OPCODE is given to the control logic, which take care of activating certain control signals
  //   - BSEL selects the constant embedded in instruction (0) or a register (1) as the B argument for the ALU
  //   - RA2SEL selects either instruction bits 15:11 or bits 25:21 as second read address for the register file
  //   25:21
  //   15:11
  //   - WDSEL selects PC + 4 (0), the ALU result (1), or the data read from the memory (2) as data to be written in the register file
  //   20:16
  //   - PCSEL  selects the next PC value: either PC + 4 (0), the sum 4 * SXT(literal) with PC + 4 (1) or the first output (JT) of the register file (2)
  //   15:11
  //   25:21
  //   15:0
  //   31:26
  //   1:0
  //   3:3
  //   6:6
  //   7:7
  //   11:8
  //   2:2
  //   5:4
endmodule

module _4 (
  input  [31:0] in,
  output [31:0] out
);

  Adder #(.width(32)) adder_1 (.a(in), .b(32'h4), .out(out));  // open: cin, cout

  // Notes on the sheet:
  //   +4
endmodule

module control_logic (
  input  [5:0] Opcode,
  input  Z,
  output [11:0] Out
);

  wire [0:0] not_1_out;
  wire [1:0] comparator_1_eq;
  wire [11:0] rom_1_data;

  Comparator #(.width(6)) comparator_1 (.a(Opcode), .b(6'b011101), .eq(comparator_1_eq[0]));  // open: gt, lt
  Comparator #(.width(6)) comparator_2 (.a(6'b011110), .b(Opcode), .eq(comparator_1_eq[1]));  // open: gt, lt
  ROM #(.addrWidth(6), .dataWidth(12)) rom_1 (.addr(Opcode), .data(rom_1_data));  // open: sel
  not not_1 (not_1_out[0], Z);
  Multiplexer #(.select(2), .width(12), .enable("false")) multiplexer_1 (
    .in0(rom_1_data), .in1({rom_1_data[11:2], 1'b0, Z}), .in2({rom_1_data[11:2], 1'b0, not_1_out[0]}),
    .out(Out), .sel(comparator_1_eq));  // open: in3

  // Notes on the sheet:
  //   contents of rom_1 (hex, n*v repeats v):
  //   24*0 1a0 10c 0 82 0 80 80 0 1d0 2d0 3d0 4d0 ad0 8d0 9d0 0 5d0 6d0 7d0 0 bd0 cd0 dd0 0 190 290 390
  //   490 a90 890 980 0 590 690 790 0 b90 c90 d90
endmodule

module sext (
  input  [15:0] lit,
  output [31:0] sext
);

  assign sext = {{16{lit[15]}}, lit};  // Bit_Extender bit_extender_1

  // Notes on the sheet:
  //   signed extension of bits
endmodule

module ORing_negation (
  input  [31:0] RD1,
  output Z
);

  nor nor_1 (Z, RD1[0], RD1[1], RD1[2], RD1[3], RD1[4], RD1[5], RD1[6], RD1[7], RD1[8], RD1[9], RD1[10], RD1[11], RD1[12], RD1[13], RD1[14], RD1[15], RD1[16], RD1[17], RD1[18], RD1[19], RD1[20], RD1[21], RD1[22], RD1[23], RD1[24], RD1[25], RD1[26], RD1[27], RD1[28], RD1[29], RD1[30], RD1[31]);
endmodule

module x4 (
  input  [31:0] in,
  output [31:0] out
);

  Multiplier #(.width(32)) multiplier_1 (.a(in), .b(32'h4), .out(out));  // open: cin, cout

  // Notes on the sheet:
  //   x4
endmodule

module data_memory (
  input  [31:0] Addr,
  input  [31:0] WD,
  input  R_W,
  output [31:0] RD
);

  wire Clock_out;

  Clock Clock (.out(Clock_out));
  RAM #(.dataWidth(32), .bus("separate")) ram_1 (
    .addr(Addr[9:2]), .din(WD), .data(RD), .str(R_W), .clk(Clock_out));  // open: sel, ld, clr
endmodule
